# Fritzing sketch console board (saved by Fritzing 0.8.7b)
perfboards: 1

parts:
  U1 = TLP621 [package=THT]
  R1 = Resistor [tolerance=±5% resistance=680 package=THT]  # not connected
  U2 = TLP621 [package=THT]
  R2 = Resistor [tolerance=±5% resistance=680 package=THT]
  R3 = Resistor [tolerance=±5% resistance=680 package=THT]  # not connected

nets:
  N1: U1.Pin_3, U2.Pin_4
  N2: U2.Pin_1, R2.Pin_1

notes:
  to glove box
  to cd changer
  from head unit
  switch
  power led
  usb port
  ---------------------------------------------------------------------------
  aux in
  POWER
  AUDIO
  COM
